# Fritzing sketch part4 (saved by Fritzing 0.9.3b)
breadboards: 1

parts:
  Mod1 = Raspberry Pi Pico
  LED1 = LED - 5mm [color="Green (555nm)" package="5 mm [THT]"]
  LED2 = LED - 5mm [color="Red (633nm)" package="5 mm [THT]"]
  S1 = Pushbutton [package="[SMD]"]
  J1 = Basic Servo

nets:
  N1: Mod1.pin_3, Mod1.pin_8, Mod1.pin_13, Mod1.pin_18, Mod1.pin_23, Mod1.pin_28, Mod1.pin_33, Mod1.pin_38, Mod1.pin_42, LED1.cathode, LED2.cathode, S1.Pin_1, S1.Pin_2, J1.gnd
  N2: Mod1.pin_17, LED1.anode
  N3: Mod1.pin_21, S1.Pin_3, S1.Pin_4
  N4: Mod1.pin_24, LED2.anode
  N5: Mod1.pin_36, J1.vcc
  N6: Mod1.pin_40, J1.pulse

custom parts:
  Raspberry Pi Pico: Raspberry Pi Pico. Based around the RP2040 microcontroller the Pico is a low cost microcontroller device bringing Raspberry Pi quality, cost, and easy of use to the microcontroller space. Jan 2021, Split part in to two versions: tht (this one) and SMD. This one will drill holes for a .1 in header in pcb to allow plugging in the module as well as providing pads to solder the module to the top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
